# Fritzing sketch Planing a LED grow light for planted aquarium (saved by Fritzing 0.7.12b)
breadboards: 1

parts:
  RED_7V-9V_1A = LED - 5mm [color="Red (660nm)" package="5 mm [THT]"]
  RED_7V-9V_1A_2 = LED - 5mm [color="Red (660nm)" package="5 mm [THT]"]
  RED_7V-9V_1A_3 = LED - 5mm [color="Red (660nm)" package="5 mm [THT]"]
  RED_7V-9V_1A_4 = LED - 5mm [color="Red (660nm)" package="5 mm [THT]"]
  White_12V_1A = LED - 5mm [color="White (8000K)" package="5 mm [THT]"]
  White_12V_1A_2 = LED - 5mm [color="White (8000K)" package="5 mm [THT]"]
  White_12V_1A_3 = LED - 5mm [color="White (8000K)" package="5 mm [THT]"]
  Arduino_Uno_R3 = Arduino
  White_12V_1A_4 = LED - 5mm [color="White (8000K)" package="5 mm [THT]"]
  Blue_10-11V_900-1000mA = LED - 5mm [color="Blue (470nm)" package="5 mm [THT]"]
  Resistor_9_1KΩ = 2.2k Ω Resistor [package=THT]
  TIP122 = NPN-Transistor [package="SOT-23 [SMD]"]
  Resistor_1KΩ = 2.2k Ω Resistor [package=THT]
  TIP122_2 = NPN-Transistor [package="SOT-23 [SMD]"]
  Resistor_1KΩ_2 = 2.2k Ω Resistor [package=THT]
  TIP122_3 = NPN-Transistor [package="SOT-23 [SMD]"]
  Resistor_1KΩ_3 = 2.2k Ω Resistor [package=THT]
  TIP122_4 = NPN-Transistor [package="SOT-23 [SMD]"]
  Power_plug = Power plug
  Power_plug_2 = Power plug
  DS1307 = DS1307 [package=THT]
  APC-25-1050 = APC-25-1050
  White_12V_1A_5 = LED - 5mm [color="White (8000K)" package="5 mm [THT]"]
  APC-35-1050 = APC-35-1050
  Power_plug_3 = Power plug
  LPC-60-1050 = LPC-60-1050
  LPC-60-1050_2 = LPC-60-1050
  Power_plug_4 = Power plug
  DS18B20_Temp_Sensor = LM35 Temperature Sensor [package="TO92 [THT]"]
  Resistor_4_7KΩ = 2.2k Ω Resistor [package=THT]
  Blue_10-11V_900-1000mA_2 = LED - 5mm [color="Blue (470nm)" package="5 mm [THT]"]
  LCD_16x2 = LCD screen
  Trimmer_Potentiometer_25KΩ = Trimmer Potentiometer [package=THT]
  FAN_12V_DC_0_14A = DC Motor
  FAN_12V_DC_0_14A_2 = DC Motor
  FAN_12V_DC_0_14A_3 = DC Motor
  Resistor_1KΩ_4 = 2.2k Ω Resistor [package=THT]
  TIP122_5 = NPN-Transistor [package="SOT-23 [SMD]"]

nets:
  N1: RED_7V-9V_1A.cathode, TIP122_3.1
  N2: RED_7V-9V_1A.anode, RED_7V-9V_1A_2.cathode
  N3: RED_7V-9V_1A_2.anode, RED_7V-9V_1A_3.cathode
  N4: RED_7V-9V_1A_3.anode, RED_7V-9V_1A_4.cathode
  N5: RED_7V-9V_1A_4.anode, LPC-60-1050_2.SDA
  N6: White_12V_1A.cathode, TIP122_4.1
  N7: White_12V_1A.anode, White_12V_1A_2.cathode
  N8: White_12V_1A_2.anode, White_12V_1A_3.cathode
  N9: White_12V_1A_3.anode, LPC-60-1050.SDA
  GND: Arduino_Uno_R3.GND, TIP122.2, TIP122_2.2, TIP122_3.2, TIP122_4.2, DS1307.0V, APC-25-1050.SCL, APC-35-1050.SCL, LPC-60-1050.SCL, LPC-60-1050_2.SCL, DS18B20_Temp_Sensor.GND, LCD_16x2.VSS, LCD_16x2.R/W, LCD_16x2.LED-, Trimmer_Potentiometer_25KΩ.leg2, TIP122_5.2
  N10: Arduino_Uno_R3.D13, LCD_16x2.RS
  N11: Arduino_Uno_R3.D12, LCD_16x2.E
  N12: Arduino_Uno_R3.D11, Resistor_1KΩ_4.Pin_0
  N13: Arduino_Uno_R3.D10, Resistor_1KΩ_2.Pin_0
  N14: Arduino_Uno_R3.D9, Resistor_1KΩ_3.Pin_0
  N15: Arduino_Uno_R3.D8, LCD_16x2.DB4
  N16: Arduino_Uno_R3.D7, LCD_16x2.DB5
  N17: Arduino_Uno_R3.D6, Resistor_1KΩ.Pin_0
  N18: Arduino_Uno_R3.D5, Resistor_9_1KΩ.Pin_0
  N19: Arduino_Uno_R3.D4, LCD_16x2.DB6
  N20: Arduino_Uno_R3.D3, LCD_16x2.DB7
  N21: Arduino_Uno_R3.D2, DS18B20_Temp_Sensor.Vout, Resistor_4_7KΩ.Pin_1
  +5V: Arduino_Uno_R3.+5V, DS1307.+V, DS18B20_Temp_Sensor.+Vs, Resistor_4_7KΩ.Pin_0, LCD_16x2.VDD, LCD_16x2.LED+, Trimmer_Potentiometer_25KΩ.leg1, FAN_12V_DC_0_14A.pin_1, FAN_12V_DC_0_14A_2.pin_1, FAN_12V_DC_0_14A_3.pin_1
  N22: Arduino_Uno_R3.A4, DS1307.SCL_-_I2C_Clock
  N23: Arduino_Uno_R3.A5, DS1307.SDA_-_I2C_Data
  N24: White_12V_1A_4.cathode, TIP122_2.1
  N25: White_12V_1A_4.anode, White_12V_1A_5.cathode
  N26: Blue_10-11V_900-1000mA.cathode, TIP122.1
  N27: Blue_10-11V_900-1000mA.anode, Blue_10-11V_900-1000mA_2.cathode
  N28: Resistor_9_1KΩ.Pin_1, TIP122.0
  N29: Resistor_1KΩ.Pin_1, TIP122_2.0
  N30: Resistor_1KΩ_2.Pin_1, TIP122_3.0
  N31: Resistor_1KΩ_3.Pin_1, TIP122_4.0
  VCC: Power_plug.VCC, LPC-60-1050.VCC
  GND_2: Power_plug.GND, LPC-60-1050.GND
  VCC_2: Power_plug_2.VCC, APC-25-1050.VCC
  GND_3: Power_plug_2.GND, APC-25-1050.GND
  N32: APC-25-1050.SDA, Blue_10-11V_900-1000mA_2.anode
  N33: White_12V_1A_5.anode, APC-35-1050.SDA
  GND_4: APC-35-1050.GND, Power_plug_3.GND
  VCC_3: APC-35-1050.VCC, Power_plug_3.VCC
  GND_5: LPC-60-1050_2.GND, Power_plug_4.GND
  VCC_4: LPC-60-1050_2.VCC, Power_plug_4.VCC
  N34: LCD_16x2.V0, Trimmer_Potentiometer_25KΩ.wiper
  N35: FAN_12V_DC_0_14A.pin_2, FAN_12V_DC_0_14A_2.pin_2, FAN_12V_DC_0_14A_3.pin_2, TIP122_5.1
  N36: Resistor_1KΩ_4.Pin_1, TIP122_5.0

custom parts:
  APC-25-1050: Description: The 9DOF Sensor stick is a very small sensor board with 9 degrees of freedom. It includes the ADXL345 accelerometer, the HMC5883L magnetometer, and the ITG-3200 gyro. The 'stick' has a simple I2C interface and a mounting hole for attaching it to your project. Also, the board is a mere 0.036" thick (0.093" overall), allowing it to be easily mounted in just about any application.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
  APC-35-1050: Description: The 9DOF Sensor stick is a very small sensor board with 9 degrees of freedom. It includes the ADXL345 accelerometer, the HMC5883L magnetometer, and the ITG-3200 gyro. The 'stick' has a simple I2C interface and a mounting hole for attaching it to your project. Also, the board is a mere 0.036" thick (0.093" overall), allowing it to be easily mounted in just about any application.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
  LPC-60-1050: Description: The 9DOF Sensor stick is a very small sensor board with 9 degrees of freedom. It includes the ADXL345 accelerometer, the HMC5883L magnetometer, and the ITG-3200 gyro. The 'stick' has a simple I2C interface and a mounting hole for attaching it to your project. Also, the board is a mere 0.036" thick (0.093" overall), allowing it to be easily mounted in just about any application.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
